// Logisim project 22121444_CPU.circ as structural Verilog: 3 circuits, main circuit main
module main (
  input  [7:0] Testing_Data,
  input  OE_TESTING,
  input  in_3,
  input  [3:0] in_4,
  input  reset_mar,
  input  reset_ir,
  input  reset_ra,
  input  Ctrl,
  input  reset_mbr,
  input  [4:0] Selectors,
  input  reset_rb,
  input  reset,
  output [3:0] counter_content,
  output [3:0] out_14,
  output [7:0] out_15,
  output [7:0] out_16,
  output [7:0] out_17,
  output [7:0] out_18,
  output out_19,
  output [2:0] sc_content,
  output [7:0] out_21,
  output [7:0] out_22
);

  wire CLK_out, cu_1_c0, cu_1_c1, cu_1_c2, cu_1_c3, cu_1_c5, instruction_register_p1,
       instruction_register_p2, MAR_p1, MAR_p2, MBR_p1, MBR_p2, Output_Register_p1, Output_Register_p2,
       register_A_p1, register_B_p1, register_B_p2;
  wire [3:0] bitselector_2_out, controlled_buffer_1_out, MAR_p6;
  wire [7:0] bit_extender_1_out, bit_extender_2_out, instruction_register_p4, instruction_register_p6,
       ram_1_dout;
  wire [31:0] decimal_decoder_64331049_1_dout, decimal_decoder_64331049_2_dout,
       decimal_decoder_64331049_3_dout, decimal_decoder_64331049_4_dout, decimal_decoder_64331049_5_dout;

  Clock CLK (.out(CLK_out));
  assign bit_extender_1_out = {{4{counter_content[3]}}, counter_content};  // Bit_Extender bit_extender_1
  Counter #(.max('h3), .width(4)) Program_Counter_25da0db7 (
    .count(cu_1_c1), .clk(CLK_out), .D(controlled_buffer_1_out), .Q(counter_content));  // open: clr, load, up, carry
  Decimal_Decoder_64331049 decimal_decoder_64331049_1 (
    .Din(bit_extender_1_out), .Dout(decimal_decoder_64331049_1_dout));
  Decimal_Decoder_64331049 decimal_decoder_64331049_2 (.Din(out_16), .Dout(decimal_decoder_64331049_2_dout));
  Decimal_Decoder_64331049 decimal_decoder_64331049_3 (.Din(out_21), .Dout(decimal_decoder_64331049_3_dout));
  _7_Segment_Display u_7_segment_display_1 (
    .g(decimal_decoder_64331049_1_dout[3]), .f(decimal_decoder_64331049_1_dout[2]),
    .a(decimal_decoder_64331049_1_dout[1]), .b(decimal_decoder_64331049_1_dout[0]),
    .e(decimal_decoder_64331049_1_dout[19]), .d(decimal_decoder_64331049_1_dout[18]),
    .c(decimal_decoder_64331049_1_dout[17]), .dp(decimal_decoder_64331049_1_dout[16]));
  assign controlled_buffer_1_out = cu_1_c0 ? counter_content : 4'bz;  // Controlled_Buffer controlled_buffer_1
  // eight_bit_memory instruction_register: pin names not known; wires that end beside it: instruction_register_p1, instruction_register_p2, reset_ir, instruction_register_p4, CLK_out, instruction_register_p6, out_15
  // eight_bit_memory register_A: pin names not known; wires that end beside it: register_A_p1, reset_ra, instruction_register_p4, CLK_out, out_16
  // eight_bit_memory register_B: pin names not known; wires that end beside it: register_B_p1, register_B_p2, reset_rb, Selectors, instruction_register_p4, CLK_out, out_21, out_19
  _7_Segment_Display u_7_segment_display_2 (
    .g(decimal_decoder_64331049_2_dout[15]), .f(decimal_decoder_64331049_2_dout[14]),
    .a(decimal_decoder_64331049_2_dout[13]), .b(decimal_decoder_64331049_2_dout[12]),
    .e(decimal_decoder_64331049_2_dout[31]), .d(decimal_decoder_64331049_2_dout[30]),
    .c(decimal_decoder_64331049_2_dout[29]), .dp(decimal_decoder_64331049_2_dout[28]));
  _7_Segment_Display u_7_segment_display_3 (
    .g(decimal_decoder_64331049_3_dout[15]), .f(decimal_decoder_64331049_3_dout[14]),
    .a(decimal_decoder_64331049_3_dout[13]), .b(decimal_decoder_64331049_3_dout[12]),
    .e(decimal_decoder_64331049_3_dout[31]), .d(decimal_decoder_64331049_3_dout[30]),
    .c(decimal_decoder_64331049_3_dout[29]), .dp(decimal_decoder_64331049_3_dout[28]));
  BitSelector #(.group(4)) bitselector_1 (.in(instruction_register_p6), .out(controlled_buffer_1_out), .sel(1'b0));
  // _22012574_ALU_main ALU: pin names not known; wires that end beside it: out_16, out_21, Ctrl, instruction_register_p4, out_18
  _7_Segment_Display u_7_segment_display_4 (
    .g(decimal_decoder_64331049_2_dout[11]), .f(decimal_decoder_64331049_2_dout[10]),
    .a(decimal_decoder_64331049_2_dout[9]), .b(decimal_decoder_64331049_2_dout[8]),
    .e(decimal_decoder_64331049_2_dout[27]), .d(decimal_decoder_64331049_2_dout[26]),
    .c(decimal_decoder_64331049_2_dout[25]), .dp(decimal_decoder_64331049_2_dout[24]));
  _7_Segment_Display u_7_segment_display_5 (
    .g(decimal_decoder_64331049_2_dout[7]), .f(decimal_decoder_64331049_2_dout[6]),
    .a(decimal_decoder_64331049_2_dout[5]), .b(decimal_decoder_64331049_2_dout[4]),
    .e(decimal_decoder_64331049_2_dout[23]), .d(decimal_decoder_64331049_2_dout[22]),
    .c(decimal_decoder_64331049_2_dout[21]), .dp(decimal_decoder_64331049_2_dout[20]));
  _7_Segment_Display u_7_segment_display_6 (
    .g(decimal_decoder_64331049_3_dout[11]), .f(decimal_decoder_64331049_3_dout[10]),
    .a(decimal_decoder_64331049_3_dout[9]), .b(decimal_decoder_64331049_3_dout[8]),
    .e(decimal_decoder_64331049_3_dout[27]), .d(decimal_decoder_64331049_3_dout[26]),
    .c(decimal_decoder_64331049_3_dout[25]), .dp(decimal_decoder_64331049_3_dout[24]));
  _7_Segment_Display u_7_segment_display_7 (
    .g(decimal_decoder_64331049_3_dout[7]), .f(decimal_decoder_64331049_3_dout[6]),
    .a(decimal_decoder_64331049_3_dout[5]), .b(decimal_decoder_64331049_3_dout[4]),
    .e(decimal_decoder_64331049_3_dout[23]), .d(decimal_decoder_64331049_3_dout[22]),
    .c(decimal_decoder_64331049_3_dout[21]), .dp(decimal_decoder_64331049_3_dout[20]));
  _7_Segment_Display u_7_segment_display_8 (
    .g(decimal_decoder_64331049_2_dout[3]), .f(decimal_decoder_64331049_2_dout[2]),
    .a(decimal_decoder_64331049_2_dout[1]), .b(decimal_decoder_64331049_2_dout[0]),
    .e(decimal_decoder_64331049_2_dout[19]), .d(decimal_decoder_64331049_2_dout[18]),
    .c(decimal_decoder_64331049_2_dout[17]), .dp(decimal_decoder_64331049_2_dout[16]));
  _7_Segment_Display u_7_segment_display_9 (
    .g(decimal_decoder_64331049_3_dout[3]), .f(decimal_decoder_64331049_3_dout[2]),
    .a(decimal_decoder_64331049_3_dout[1]), .b(decimal_decoder_64331049_3_dout[0]),
    .e(decimal_decoder_64331049_3_dout[19]), .d(decimal_decoder_64331049_3_dout[18]),
    .c(decimal_decoder_64331049_3_dout[17]), .dp(decimal_decoder_64331049_3_dout[16]));
  LED led_1 (.in(instruction_register_p4[7]));
  LED led_2 (.in(instruction_register_p4[6]));
  LED led_3 (.in(instruction_register_p4[5]));
  assign instruction_register_p4 = OE_TESTING ? Testing_Data : 8'bz;  // Controlled_Buffer controlled_buffer_2
  LED led_4 (.in(instruction_register_p4[4]));
  LED led_5 (.in(instruction_register_p4[3]));
  LED led_6 (.in(instruction_register_p4[2]));
  LED led_7 (.in(instruction_register_p4[1]));
  LED led_8 (.in(instruction_register_p4[0]));
  // eight_bit_memory Output_Register: pin names not known; wires that end beside it: Output_Register_p1, Output_Register_p2, reset, instruction_register_p4, CLK_out, instruction_register_p4, out_22
  Decimal_Decoder_64331049 decimal_decoder_64331049_4 (.Din(out_22), .Dout(decimal_decoder_64331049_4_dout));
  // four_bit_memory MAR: pin names not known; wires that end beside it: MAR_p1, MAR_p2, controlled_buffer_1_out, reset_mar, CLK_out, MAR_p6, out_14
  assign instruction_register_p4 = cu_1_c5 ? out_17 : 8'bz;  // Controlled_Buffer controlled_buffer_3
  // eight_bit_memory MBR: pin names not known; wires that end beside it: MBR_p1, MBR_p2, reset_mbr, instruction_register_p4, CLK_out, instruction_register_p4, out_17
  assign MAR_p6 = in_3 ? in_4 : 4'bz;  // Controlled_Buffer controlled_buffer_4
  _7_Segment_Display u_7_segment_display_10 (
    .g(decimal_decoder_64331049_4_dout[15]), .f(decimal_decoder_64331049_4_dout[14]),
    .a(decimal_decoder_64331049_4_dout[13]), .b(decimal_decoder_64331049_4_dout[12]),
    .e(decimal_decoder_64331049_4_dout[31]), .d(decimal_decoder_64331049_4_dout[30]),
    .c(decimal_decoder_64331049_4_dout[29]), .dp(decimal_decoder_64331049_4_dout[28]));
  _7_Segment_Display u_7_segment_display_11 (
    .g(decimal_decoder_64331049_4_dout[11]), .f(decimal_decoder_64331049_4_dout[10]),
    .a(decimal_decoder_64331049_4_dout[9]), .b(decimal_decoder_64331049_4_dout[8]),
    .e(decimal_decoder_64331049_4_dout[27]), .d(decimal_decoder_64331049_4_dout[26]),
    .c(decimal_decoder_64331049_4_dout[25]), .dp(decimal_decoder_64331049_4_dout[24]));
  LED led_9 (.in(instruction_register_p4[7]));
  LED led_10 (.in(instruction_register_p4[6]));
  LED led_11 (.in(instruction_register_p4[5]));
  LED led_12 (.in(instruction_register_p4[4]));
  _7_Segment_Display u_7_segment_display_12 (
    .g(decimal_decoder_64331049_4_dout[7]), .f(decimal_decoder_64331049_4_dout[6]),
    .a(decimal_decoder_64331049_4_dout[5]), .b(decimal_decoder_64331049_4_dout[4]),
    .e(decimal_decoder_64331049_4_dout[23]), .d(decimal_decoder_64331049_4_dout[22]),
    .c(decimal_decoder_64331049_4_dout[21]), .dp(decimal_decoder_64331049_4_dout[20]));
  _7_Segment_Display u_7_segment_display_13 (
    .g(decimal_decoder_64331049_4_dout[3]), .f(decimal_decoder_64331049_4_dout[2]),
    .a(decimal_decoder_64331049_4_dout[1]), .b(decimal_decoder_64331049_4_dout[0]),
    .e(decimal_decoder_64331049_4_dout[19]), .d(decimal_decoder_64331049_4_dout[18]),
    .c(decimal_decoder_64331049_4_dout[17]), .dp(decimal_decoder_64331049_4_dout[16]));
  LED led_13 (.in(instruction_register_p4[3]));
  LED led_14 (.in(instruction_register_p4[2]));
  LED led_15 (.in(instruction_register_p4[1]));
  LED led_16 (.in(instruction_register_p4[0]));
  assign instruction_register_p4 = cu_1_c3 ? ~ram_1_dout : 8'bz;  // Controlled_Inverter controlled_inverter_1
  Counter #(.max('h5), .width(3)) Step_counter (.clk(CLK_out), .Q(sc_content));  // open: clr, load, up, count, D, carry
  RAM #(.addrWidth(4), .enables("line")) ram_1 (
    .addr(MAR_p6), .we(cu_1_c2), .clk(CLK_out), .din(instruction_register_p4), .dout(ram_1_dout));
  BitSelector #(.group(4)) bitselector_2 (.in(out_15), .out(bitselector_2_out), .sel(1'b1));
  assign bit_extender_2_out = {{5{1'b0}}, sc_content};  // Bit_Extender bit_extender_2
  Decimal_Decoder_64331049 decimal_decoder_64331049_5 (
    .Din(bit_extender_2_out), .Dout(decimal_decoder_64331049_5_dout));
  CU cu_1 (
    .OPC3(bitselector_2_out[3]), .OPC2(bitselector_2_out[2]), .OPC1(bitselector_2_out[1]),
    .OPC0(bitselector_2_out[0]), .SC2(sc_content[2]), .SC1(sc_content[1]), .SC0(sc_content[0]), .C0(cu_1_c0),
    .C1(cu_1_c1), .C2(cu_1_c2), .C3(cu_1_c3), .C4(MBR_p1), .C5(cu_1_c5), .C6(MBR_p2),
    .C7(instruction_register_p1), .C8(instruction_register_p2), .C9(MAR_p1), .C10(MAR_p2),
    .C11(register_B_p1), .C12(register_A_p1), .C13(register_B_p2), .C14(Output_Register_p2),
    .C15(Output_Register_p1));
  _7_Segment_Display u_7_segment_display_14 (
    .g(decimal_decoder_64331049_5_dout[3]), .f(decimal_decoder_64331049_5_dout[2]),
    .a(decimal_decoder_64331049_5_dout[1]), .b(decimal_decoder_64331049_5_dout[0]),
    .e(decimal_decoder_64331049_5_dout[19]), .d(decimal_decoder_64331049_5_dout[18]),
    .c(decimal_decoder_64331049_5_dout[17]), .dp(decimal_decoder_64331049_5_dout[16]));

  // Notes on the sheet:
  //   Register A
  //   Register B
  //   Internal Address Bus
  //   Internal Data Bus
  //   External Address Bus
  //   External Data Bus
  //   Output Register
  //   pc_oe
  //   pc_count_enable
  //   ram we
  //   ram oe
  //   mbr we
  //   mbr internal bus enable
  //   mbr oe
  //   ir we
  //   ir oe
  //   mar we
  //   mar oe
  //   ALU oe
  //   Reg_A we
  //   Reg_B we
  //   Output register Oe
  //   Output register we
endmodule

module Decimal_Decoder_64331049 (
  input  [7:0] Din,
  output [31:0] Dout
);

  ROM #(.dataWidth(32)) rom_1 (
    .addr(Din),
    .data({Dout[31:28], Dout[15:12], Dout[27:24], Dout[11:8], Dout[23:20], Dout[7:4], Dout[19:16], Dout[3:0]}));

  // Notes on the sheet:
  //   contents of rom_1 (hex, n*v repeats v):
  //   e7 21 cb 6b 2d 6e ee 23 ef 2f 21e7 2121 21cb 216b 212d 216e 21ee 2123 21ef 212f cbe7 cb21 cbcb cb6b
  //   cb2d cb6e cbee cb23 cbef cb2f 6be7 6b21 6bcb 6b6b 6b2d 6b6e 6bee 6b23 6bef 6b2f 2de7 2d21 2dcb 2d6b
  //   2d2d 2d6e 2dee 2d23 2def 2d2f 6ee7 6e21 6ecb 6e6b 6e2d 6e6e 6eee 6e23 6eef 6e2f eee7 ee21 eecb ee6b
  //   ee2d ee6e eeee ee23 eeef ee2f 23e7 2321 23cb 236b 232d 236e 23ee 2323 23ef 232f efe7 ef21 efcb ef6b
  //   ef2d ef6e efee ef23 efef ef2f 2fe7 2f21 2fcb 2f6b 2f2d 2f6e 2fee 2f23 2fef 2f2f 21e7e7 21e721 21e7cb
  //   21e76b 21e72d 21e76e 21e7ee 21e723 21e7ef 21e72f 2121e7 212121 2121cb 21216b 21212d 21216e 2121ee
  //   212123 2121ef 21212f 21cbe7 21cb21 21cbcb 21cb6b 21cb2d 21cb6e 21cbee 21cb23 21cbef 21cb2f 216be7
  //   216b21 216bcb 216b6b 216b2d 216b6e 216bee 216b23 216bef 216b2f 212de7 212d21 212dcb 212d6b 212d2d
  //   212d6e 212dee 212d23 212def 212d2f 216ee7 216e21 216ecb 216e6b 216e2d 216e6e 216eee 216e23 216eef
  //   216e2f 21eee7 21ee21 21eecb 21ee6b 21ee2d 21ee6e 21eeee 21ee23 21eeef 21ee2f 2123e7 212321 2123cb
  //   21236b 21232d 21236e 2123ee 212323 2123ef 21232f 21efe7 21ef21 21efcb 21ef6b 21ef2d 21ef6e 21efee
  //   21ef23 21efef 21ef2f 212fe7 212f21 212fcb 212f6b 212f2d 212f6e 212fee 212f23 212fef 212f2f cbe7e7
  //   cbe721 cbe7cb cbe76b cbe72d cbe76e cbe7ee cbe723 cbe7ef cbe72f cb21e7 cb2121 cb21cb cb216b cb212d
  //   cb216e cb21ee cb2123 cb21ef cb212f cbcbe7 cbcb21 cbcbcb cbcb6b cbcb2d cbcb6e cbcbee cbcb23 cbcbef
  //   cbcb2f cb6be7 cb6b21 cb6bcb cb6b6b cb6b2d cb6b6e cb6bee cb6b23 cb6bef cb6b2f cb2de7 cb2d21 cb2dcb
  //   cb2d6b cb2d2d cb2d6e cb2dee cb2d23 cb2def cb2d2f cb6ee7 cb6e21 cb6ecb cb6e6b cb6e2d cb6e6e
endmodule

module CU (
  input  OPC3,
  input  OPC2,
  input  OPC1,
  input  OPC0,
  input  SC2,
  input  SC1,
  input  SC0,
  output C0,
  output C1,
  output C2,
  output C3,
  output C4,
  output C5,
  output C6,
  output C7,
  output C8,
  output C9,
  output C10,
  output C11,
  output C12,
  output C13,
  output C14,
  output C15
);

  wire and_4_out, and_5_out, and_6_out, and_7_out, and_8_out, and_9_out, and_10_out, and_13_out, and_14_out,
       and_15_out, and_16_out, and_17_out, and_18_out, and_19_out, and_20_out, not_1_out, not_2_out,
       not_3_out, not_4_out, not_5_out;

  not not_1 (not_1_out, OPC1);
  not not_2 (not_2_out, OPC0);
  not not_3 (not_3_out, SC2);
  not not_4 (not_4_out, SC1);
  not not_5 (not_5_out, SC0);
  and and_1 (C0, not_3_out, not_4_out, not_5_out);
  and and_2 (C1, not_3_out, not_4_out, SC0);
  and and_3 (C2, OPC1, OPC0, SC2, not_4_out, not_5_out);
  and and_4 (and_4_out, not_3_out, not_4_out, SC0);
  and and_5 (and_5_out, not_1_out, SC2, not_4_out, not_5_out);
  and and_6 (and_6_out, not_3_out, not_4_out, SC0);
  and and_7 (and_7_out, not_1_out, SC2, not_4_out, not_5_out);
  and and_8 (and_8_out, OPC1, OPC0, not_3_out, SC0);
  and and_9 (and_9_out, not_3_out, SC1, not_5_out);
  and and_10 (and_10_out, not_1_out, SC2, not_4_out, SC0);
  and and_11 (C6, OPC1, OPC0, SC2, not_4_out, not_5_out);
  and and_12 (C7, not_3_out, SC1, not_5_out);
  and and_13 (and_13_out, not_1_out, not_3_out, SC1, SC0);
  and and_14 (and_14_out, OPC0, not_3_out, SC1, SC0);
  and and_15 (and_15_out, not_3_out, not_4_out, not_5_out);
  and and_16 (and_16_out, not_1_out, not_3_out, SC1, SC0);
  and and_17 (and_17_out, OPC0, not_3_out, SC1, SC0);
  and and_18 (and_18_out, not_3_out, not_4_out, SC0);
  and and_19 (and_19_out, not_1_out, SC2, not_4_out, not_5_out);
  and and_20 (and_20_out, OPC0, SC2, not_4_out, not_5_out);
  and and_21 (C11, OPC1, not_2_out, not_3_out, SC1, SC0);
  and and_22 (C12, not_1_out, not_2_out, SC2, not_4_out, SC0);
  and and_23 (C13, not_1_out, OPC0, SC2, not_4_out, SC0);
  and and_24 (C14, OPC1, OPC0, not_3_out, SC1, SC0);
  and and_25 (C15, OPC1, not_2_out, not_3_out, SC1, SC0);
  or or_1 (C3, and_4_out, and_5_out);
  or or_2 (C4, and_6_out, and_7_out, and_8_out);
  or or_3 (C5, and_9_out, and_10_out);
  or or_4 (C8, and_13_out, and_14_out);
  or or_5 (C9, and_15_out, and_16_out, and_17_out);
  or or_6 (C10, and_18_out, and_19_out, and_20_out);
endmodule
