// Logisim project 22121444_mem.circ as structural Verilog: 3 circuits, main circuit one_bit_memory
module one_bit_memory (
  input  Clock,
  input  WE,
  input  Din,
  input  OE,
  input  Reset,
  output Dout,
  output Stored_Data
);

  wire and_1_out, and_2_out, not_1_out, or_1_out;

  not not_1 (not_1_out, WE);
  and and_1 (and_1_out, Stored_Data, not_1_out);
  and and_2 (and_2_out, WE, Din);
  or or_1 (or_1_out, and_1_out, and_2_out);
  D_Flip_Flop d_ff_1 (.D(or_1_out), .clk(Clock), .Q(Stored_Data), .reset(Reset));  // open: Qn, preset
  assign Dout = OE ? Stored_Data : 1'bz;  // Controlled_Buffer controlled_buffer_1
endmodule

module four_bit_memory (
  input  [3:0] Din,
  input  WE,
  input  OE,
  input  Reset,
  input  Clock,
  output [3:0] Dout,
  output [3:0] Stored_Bits
);

  one_bit_memory one_bit_memory_1 (
    .WE(WE), .Din(Din[3]), .OE(OE), .Reset(Reset), .Clock(Clock), .Stored_Data(Stored_Bits[3]), .Dout(Dout[3]));
  one_bit_memory one_bit_memory_2 (
    .WE(WE), .Din(Din[2]), .OE(OE), .Reset(Reset), .Clock(Clock), .Stored_Data(Stored_Bits[2]), .Dout(Dout[2]));
  one_bit_memory one_bit_memory_3 (
    .WE(WE), .Din(Din[1]), .OE(OE), .Reset(Reset), .Clock(Clock), .Stored_Data(Stored_Bits[1]), .Dout(Dout[1]));
  one_bit_memory one_bit_memory_4 (
    .WE(WE), .Din(Din[0]), .OE(OE), .Reset(Reset), .Clock(Clock), .Stored_Data(Stored_Bits[0]), .Dout(Dout[0]));
endmodule

module eight_bit_memory (
  input  [7:0] Din,
  input  We,
  input  OE,
  input  Reset,
  input  Clock,
  output [7:0] Stored_Bits,
  output [7:0] Dout
);

  four_bit_memory four_bit_memory_1 (
    .WE(We), .OE(OE), .Reset(Reset), .Clock(Clock), .Din(Din[7:4]), .Dout(Dout[7:4]),
    .Stored_Bits(Stored_Bits[7:4]));
  four_bit_memory four_bit_memory_2 (
    .WE(We), .OE(OE), .Reset(Reset), .Clock(Clock), .Din(Din[3:0]), .Dout(Dout[3:0]),
    .Stored_Bits(Stored_Bits[3:0]));
endmodule
