// Logisim project CPU.circ as structural Verilog: 3 circuits, main circuit main
module main (
);

  IR ir_1 ();  // open: in_1, we, clk, reset, out_5
  datapath MAR ();  // open: in_1, we, clk, reset, out_5
endmodule

module datapath (
  input  [7:0] in_1,
  input  we,
  input  clk,
  input  reset,
  output [7:0] out_5
);

  Register register_1 (.D(in_1), .en(we), .clk(clk), .Q(out_5), .clr(reset));
endmodule

module IR (
  input  [15:0] in_1,
  input  we,
  input  clk,
  input  reset,
  output [15:0] out_5
);

  Register #(.width(16)) register_1 (.D(in_1), .en(we), .clk(clk), .Q(out_5), .clr(reset));
endmodule
